// Logisim project test001.circ as structural Verilog: 1 circuit, main circuit main
module main (
  input  [3:0] \input ,
  output [3:0] result_of_add,
  output output_of_C
);

  wire adder_1_cout, and_1_out, and_2_out, and_3_out, and_4_out, and_5_out, and_6_out, clock_1_out,
       clock_2_out, d_ff_1_q, d_ff_1_qn, d_ff_2_q, d_ff_2_qn, nor_1_out, or_1_out, or_2_out, or_3_out,
       xor_1_out;
  wire [3:0] register_1_q, register_2_q;

  Clock clock_1 (.out(clock_1_out));
  or or_1 (or_1_out, d_ff_2_qn, d_ff_1_qn);
  or or_2 (or_2_out, d_ff_1_q, d_ff_2_q);
  D_Flip_Flop d_ff_1 (.clk(clock_1_out), .D(or_1_out), .Q(d_ff_1_q), .Qn(d_ff_1_qn), .en(1'b1));  // open: preset, reset
  D_Flip_Flop d_ff_2 (.clk(clock_1_out), .D(or_2_out), .Q(d_ff_2_q), .Qn(d_ff_2_qn), .en(1'b1));  // open: preset, reset
  and and_1 (and_1_out, d_ff_2_qn, d_ff_1_qn);
  or or_3 (or_3_out, and_1_out, and_2_out);
  and and_2 (and_2_out, d_ff_2_q, d_ff_1_q);
  xor xor_1 (xor_1_out, d_ff_2_q, d_ff_1_q);
  and and_3 (and_3_out, d_ff_1_qn, d_ff_2_q);
  nor nor_1 (nor_1_out, d_ff_2_q, d_ff_1_q);
  Clock clock_2 (.out(clock_2_out));
  and and_4 (and_4_out, or_3_out, clock_2_out);
  and and_5 (and_5_out, clock_2_out, xor_1_out);
  and and_6 (and_6_out, and_3_out, clock_2_out);
  Register #(.width(4)) register_1 (.D(\input ), .en(1'b1), .Q(register_1_q), .clk(and_4_out));  // open: clr
  Register #(.width(4)) register_2 (.D(result_of_add), .en(1'b1), .Q(register_2_q), .clk(and_5_out));  // open: clr
  Adder #(.width(4)) adder_1 (
    .a(register_1_q), .b(register_2_q), .out(result_of_add), .cout(adder_1_cout));  // open: cin
  Register #(.width(1), .trigger("low")) register_3 (
    .D(adder_1_cout), .en(1'b1), .Q(output_of_C), .clk(and_6_out), .clr(nor_1_out));

  // Notes on the sheet:
  //   T1
  //   1
  //   A
  //   B
  //   LDB
  //   CLR
  //   LDA
  //   ADD
  //   LDC
  //   T2
endmodule
