// Logisim project test002.circ as structural Verilog: 1 circuit, main circuit main
module main (
  input  [3:0] \input 
);

  wire and_1_out, and_2_out, and_3_out, and_4_out, clock_1_out, comparator_1_lt, d_ff_1_q, d_ff_1_qn,
       d_ff_2_q, d_ff_2_qn, or_1_out, or_2_out, xnor_1_out;
  wire [3:0] register_1_q, register_2_q;

  Clock clock_1 (.out(clock_1_out));
  and and_1 (and_1_out, and_4_out, d_ff_1_q);
  or or_1 (or_1_out, and_1_out, d_ff_2_q);
  D_Flip_Flop d_ff_1 (.clk(clock_1_out), .D(or_1_out), .Q(d_ff_1_q), .Qn(d_ff_1_qn), .en(1'b1));  // open: preset, reset
  D_Flip_Flop d_ff_2 (.clk(clock_1_out), .D(or_2_out), .Q(d_ff_2_q), .Qn(d_ff_2_qn), .en(1'b1));  // open: preset, reset
  or or_2 (or_2_out, d_ff_2_qn, d_ff_1_qn);
  xnor xnor_1 (xnor_1_out, d_ff_1_q, d_ff_2_q);
  and and_2 (and_2_out, d_ff_1_qn, d_ff_2_q);
  and and_3 (and_3_out, d_ff_1_q, d_ff_2_qn);
  Register #(.width(4)) register_1 (.D(\input ), .en(1'b1), .Q(register_1_q), .clk(xnor_1_out));  // open: clr
  Register #(.width(4)) register_2 (.D(register_1_q), .en(1'b1), .Q(register_2_q), .clk(and_2_out));  // open: clr
  and and_4 (and_4_out, and_3_out, comparator_1_lt);
  Comparator #(.width(4), .mode("unsigned")) comparator_1 (
    .a(register_1_q), .b(register_2_q), .lt(comparator_1_lt));  // open: gt, eq

  // Notes on the sheet:
  //   A
  //   B
  //   1
  //   LDRb
  //   LDRa
  //   CAP
  //   Rb
  //   Ra
endmodule
