// Logisim project test003.circ as structural Verilog: 1 circuit, main circuit main
module main (
  input  [3:0] \input ,
  input  _0,
  output [3:0] result_of_add,
  output output_of_C
);

  wire adder_1_cout, and_1_out, and_2_out, and_3_out, and_4_out, and_5_out, and_6_out, clock_1_out,
       clock_2_out, d_ff_1_qn, d_ff_2_qn, multiplexer_1_out, multiplexer_2_out, nor_1_out, or_1_out,
       xor_1_out;
  wire [1:0] d_ff_2_q;
  wire [3:0] register_1_q, register_2_q;

  Multiplexer #(.select(2)) multiplexer_1 (
    .in0(_0), .in1(1'b1), .in2(1'b1), .in3(1'b1), .out(multiplexer_1_out), .sel(d_ff_2_q), .en(1'b1));
  Multiplexer #(.select(2)) multiplexer_2 (
    .in0(1'b1), .in1(1'b1), .in2(1'b1), .in3(_0), .out(multiplexer_2_out), .sel(d_ff_2_q), .en(1'b1));
  Clock clock_1 (.out(clock_1_out));
  D_Flip_Flop d_ff_1 (
    .clk(clock_1_out), .D(multiplexer_1_out), .Q(d_ff_2_q[1]), .Qn(d_ff_1_qn), .en(1'b1));  // open: preset, reset
  D_Flip_Flop d_ff_2 (
    .clk(clock_1_out), .D(multiplexer_2_out), .Q(d_ff_2_q[0]), .Qn(d_ff_2_qn), .en(1'b1));  // open: preset, reset
  and and_1 (and_1_out, d_ff_2_qn, d_ff_1_qn);
  or or_1 (or_1_out, and_1_out, and_2_out);
  and and_2 (and_2_out, d_ff_2_q[0], d_ff_2_q[1]);
  xor xor_1 (xor_1_out, d_ff_2_q[0], d_ff_2_q[1]);
  and and_3 (and_3_out, d_ff_1_qn, d_ff_2_q[0]);
  nor nor_1 (nor_1_out, d_ff_2_q[0], d_ff_2_q[1]);
  Clock clock_2 (.out(clock_2_out));
  and and_4 (and_4_out, or_1_out, clock_2_out);
  and and_5 (and_5_out, clock_2_out, xor_1_out);
  and and_6 (and_6_out, and_3_out, clock_2_out);
  Register #(.width(4)) register_1 (.D(\input ), .en(1'b1), .Q(register_1_q), .clk(and_4_out));  // open: clr
  Register #(.width(4)) register_2 (.D(result_of_add), .en(1'b1), .Q(register_2_q), .clk(and_5_out));  // open: clr
  Adder #(.width(4)) adder_1 (
    .a(register_1_q), .b(register_2_q), .out(result_of_add), .cout(adder_1_cout));  // open: cin
  Register #(.width(1), .trigger("low")) register_3 (
    .D(adder_1_cout), .en(1'b1), .Q(output_of_C), .clk(and_6_out), .clr(nor_1_out));

  // Notes on the sheet:
  //   1
  //   T1
  //   A
  //   B
  //   LDA
  //   LDB
  //   ADD
  //   LDC
  //   CLR
  //   T2
endmodule
