// Logisim project test004.circ as structural Verilog: 1 circuit, main circuit main
module main (
  input  [3:0] \input ,
  input  _0
);

  wire and_1_out, and_2_out, and_3_out, clock_1_out, comparator_1_lt, d_ff_1_qn, d_ff_2_qn,
       multiplexer_1_out, multiplexer_2_out, xnor_1_out;
  wire [1:0] d_ff_2_q;
  wire [3:0] register_1_q, register_2_q;

  Multiplexer #(.select(2)) multiplexer_1 (
    .in0(_0), .in1(1'b1), .in2(and_3_out), .in3(1'b1), .out(multiplexer_1_out), .sel(d_ff_2_q), .en(1'b1));
  Multiplexer #(.select(2)) multiplexer_2 (
    .in0(1'b1), .in1(1'b1), .in2(1'b1), .in3(_0), .out(multiplexer_2_out), .sel(d_ff_2_q), .en(1'b1));
  Clock clock_1 (.out(clock_1_out));
  D_Flip_Flop d_ff_1 (
    .clk(clock_1_out), .D(multiplexer_1_out), .Q(d_ff_2_q[1]), .Qn(d_ff_1_qn), .en(1'b1));  // open: preset, reset
  D_Flip_Flop d_ff_2 (
    .clk(clock_1_out), .D(multiplexer_2_out), .Q(d_ff_2_q[0]), .Qn(d_ff_2_qn), .en(1'b1));  // open: preset, reset
  xnor xnor_1 (xnor_1_out, d_ff_2_q[1], d_ff_2_q[0]);
  and and_1 (and_1_out, d_ff_1_qn, d_ff_2_q[0]);
  and and_2 (and_2_out, d_ff_2_q[1], d_ff_2_qn);
  Register #(.width(4)) register_1 (.D(\input ), .en(1'b1), .Q(register_1_q), .clk(xnor_1_out));  // open: clr
  Register #(.width(4)) register_2 (.D(register_1_q), .en(1'b1), .Q(register_2_q), .clk(and_1_out));  // open: clr
  and and_3 (and_3_out, and_2_out, comparator_1_lt);
  Comparator #(.width(4), .mode("unsigned")) comparator_1 (
    .a(register_1_q), .b(register_2_q), .lt(comparator_1_lt));  // open: gt, eq

  // Notes on the sheet:
  //   1
  //   A
  //   B
  //   LDRb
  //   LDRa
  //   CAP
  //   Rb
  //   Ra
endmodule
