// Logisim project test005.circ as structural Verilog: 1 circuit, main circuit main
module main (
  input  [3:0] \input ,
  output [3:0] result_of_add,
  output output_of_C
);

  wire a_q, a_qn, adder_1_cout, and_1_out, and_2_out, and_3_out, and_4_out, and_5_out, and_6_out, and_7_out,
       b_q, b_qn, c_q, c_qn, clock_1_out, clock_2_out, d_q, d_qn, nor_1_out, or_1_out, or_2_out, or_3_out;
  wire [3:0] register_1_q, register_2_q;

  Clock clock_1 (.out(clock_1_out));
  nor nor_1 (nor_1_out, a_q, b_q, c_q, d_q);
  or or_1 (or_1_out, and_3_out, and_2_out);
  D_Flip_Flop a (.clk(clock_1_out), .D(nor_1_out), .Q(a_q), .Qn(a_qn), .en(1'b1));  // open: preset, reset
  D_Flip_Flop b (.clk(clock_1_out), .D(and_1_out), .Q(b_q), .Qn(b_qn), .en(1'b1));  // open: preset, reset
  D_Flip_Flop c (.clk(clock_1_out), .D(or_1_out), .Q(c_q), .Qn(c_qn), .en(1'b1));  // open: preset, reset
  D_Flip_Flop d (.clk(clock_1_out), .D(and_4_out), .Q(d_q), .Qn(d_qn), .en(1'b1));  // open: preset, reset
  and and_1 (and_1_out, b_qn, c_qn, a_q, d_qn);
  and and_2 (and_2_out, a_qn, b_q, c_qn, d_qn);
  and and_3 (and_3_out, b_qn, c_qn, d_q, a_qn);
  and and_4 (and_4_out, a_qn, b_qn, c_q, d_qn);
  or or_2 (or_2_out, and_1_out, and_4_out);
  or or_3 (or_3_out, and_2_out, and_3_out);
  Clock clock_2 (.out(clock_2_out));
  and and_5 (and_5_out, or_2_out, clock_2_out);
  and and_6 (and_6_out, clock_2_out, or_3_out);
  and and_7 (and_7_out, and_3_out, clock_2_out);
  Register #(.width(4)) register_1 (.D(\input ), .en(1'b1), .Q(register_1_q), .clk(and_5_out));  // open: clr
  Register #(.width(4)) register_2 (.D(result_of_add), .en(1'b1), .Q(register_2_q), .clk(and_6_out));  // open: clr
  Adder #(.width(4)) adder_1 (
    .a(register_1_q), .b(register_2_q), .out(result_of_add), .cout(adder_1_cout));  // open: cin
  Register #(.width(1), .trigger("low")) register_3 (
    .D(adder_1_cout), .en(1'b1), .Q(output_of_C), .clk(and_7_out), .clr(and_2_out));

  // Notes on the sheet:
  //   1
  //   T1
  //   LDA
  //   LDB
  //   ADD
  //   LDC
  //   CLR
  //   T2
endmodule
