// Logisim project test006.circ as structural Verilog: 1 circuit, main circuit main
module main (
  input  [3:0] \input 
);

  wire and_1_out, and_2_out, and_3_out, b_q, c_q, clock_1_out, comparator_1_lt, d_ff_1_q, d_q, nor_1_out,
       not_1_out, or_1_out, or_2_out, or_3_out;
  wire [3:0] register_1_q, register_2_q;

  Clock clock_1 (.out(clock_1_out));
  nor nor_1 (nor_1_out, d_q, c_q, b_q, d_ff_1_q);
  or or_1 (or_1_out, and_2_out, d_ff_1_q);
  or or_2 (or_2_out, and_1_out, b_q);
  D_Flip_Flop d_ff_1 (.clk(clock_1_out), .D(nor_1_out), .Q(d_ff_1_q), .en(1'b1));  // open: Qn, preset, reset
  D_Flip_Flop b (.clk(clock_1_out), .D(or_1_out), .Q(b_q), .en(1'b1));  // open: Qn, preset, reset
  D_Flip_Flop c (.clk(clock_1_out), .D(or_2_out), .Q(c_q), .en(1'b1));  // open: Qn, preset, reset
  D_Flip_Flop d (.clk(clock_1_out), .D(c_q), .Q(d_q), .en(1'b1));  // open: Qn, preset, reset
  and and_1 (and_1_out, d_q, and_3_out);
  and and_2 (and_2_out, d_q, d_q, not_1_out);
  not not_1 (not_1_out, and_3_out);
  or or_3 (or_3_out, d_ff_1_q, c_q);
  Register #(.width(4)) register_1 (.D(\input ), .en(1'b1), .Q(register_1_q), .clk(or_3_out));  // open: clr
  Register #(.width(4)) register_2 (.D(register_1_q), .en(1'b1), .Q(register_2_q), .clk(b_q));  // open: clr
  and and_3 (and_3_out, d_q, comparator_1_lt);
  Comparator #(.width(4), .mode("unsigned")) comparator_1 (
    .a(register_1_q), .b(register_2_q), .lt(comparator_1_lt));  // open: gt, eq

  // Notes on the sheet:
  //   1
  //   a
  //   LDRb
  //   LDRa
  //   CAP
  //   Ra
  //   Rb
endmodule
